# Fritzing sketch RXimg (saved by Fritzing 0.9.3b)
breadboards: 1

parts:
  Componente1 = Arduino Nano (Rev3.0)
  Componente2 = NRF24L01
  U1 = V_REG_LD1117VXX [package=78xxl]
  C1 = Capacitor Polarized [package=cpol-radial-10uf-25v]

nets:
  GND: Componente1.GND, Componente2.GND, U1.GND, C1.-
  N1: Componente1.D7, Componente2.CE
  N2: Componente1.D8, Componente2.CSN
  N3: Componente1.D11/MOSI, Componente2.SCK
  N4: Componente1.D12/MISO, Componente2.MOSI
  N5: Componente1.D13/SCK, Componente2.MISO
  N6: Componente2.VCC, U1.OUT, C1.+
