# Fritzing sketch TXimg (saved by Fritzing 0.9.3b)
breadboards: 1

parts:
  Componente2 = NRF24L01
  U1 = V_REG_LD1117VXX [package=78xxl]
  C1 = Capacitor Polarized [package=cpol-radial-10uf-25v]
  Componente3 = Arduino Uno (Rev3)
  J1 = Basic Servo
  J2 = Basic Servo
  hc-sr1 = hc-sr04
  hc-sr2 = hc-sr04

nets:
  N1: Componente2.MOSI, Componente3.D12/MISO
  N2: Componente2.CSN, Componente3.D8
  N3: Componente2.VCC, U1.OUT, C1.+
  N4: Componente2.MISO, Componente3.D13/SCK
  N5: Componente2.SCK, Componente3.D11_PWM/MOSI
  N6: Componente2.CE, Componente3.D7
  GND: Componente2.GND, U1.GND, C1.-, Componente3.GND, J1.gnd, J2.gnd, hc-sr1.GND, hc-sr2.GND
  VCC: U1.IN, hc-sr1.VCC, hc-sr2.VCC
  N7: Componente3.D9_PWM, J1.pulse
  N8: Componente3.D10_PWM/SS, J2.pulse
  N9: Componente3.D2, hc-sr1.Echo
  N10: Componente3.D3_PWM, hc-sr1.Trig
  N11: Componente3.D4, hc-sr2.Echo
  N12: Componente3.D5_PWM, hc-sr2.Trig
  VCC_2: Componente3.5V, J1.vcc, J2.vcc
