# Fritzing sketch Sketch (saved by Fritzing 0.9.3b)
breadboards: 1

parts:
  Componente1 = Arduino Nano (Rev3.0)
  hc-sr1 = hc-sr04
  J1 = Basic Servo
  J2 = Basic Servo

nets:
  N1: Componente1.D2, hc-sr1.Trig
  N2: Componente1.D3, hc-sr1.Echo
  GND: Componente1.GND, hc-sr1.GND, J1.gnd, J2.gnd
  VCC: Componente1.5V, hc-sr1.VCC, J1.vcc, J2.vcc
